# Fritzing sketch FleeCar_Schematic (saved by Fritzing 0.9.3b)
breadboards: 1

parts:
  U2 = atmega328 [package=dip]
  IC2 = L293D [package=THT]
  IC3 = L293D [package=THT]
  R1 = Resistor [tolerance=±5% resistance=220 package=THT]
  C1 = Ceramic Capacitor [capacitance=100nF package="100 mil [THT, multilayer]"]

nets:
  N1: U2.RESET, R1.Pin_1
  N2: U2.VCC, U2.AVCC, U2.AREF, IC2.+V, IC3.+V, R1.Pin_0, C1.0
  N3: U2.GND, IC2.0V, IC3.0V, C1.1
  N4: U2.D6_(PWM), IC2.Enable_1, IC2.Enable_2, IC3.Enable_1, IC3.Enable_2
  N5: U2.D7, IC3.In_1
  N6: U2.D8, IC3.In_2
  N7: IC2.+Vmotor, IC3.+Vmotor
